# Fritzing sketch passiveArduino (saved by Fritzing 0.9.4)
breadboards: 1

parts:
  Part1 = Arduino Nano (Rev3.0)
  S1 = Momentary Switch [package=ksa_sealed_tac_switch]
  LED1 = smd LED [color="Red (633nm)" package="0805 [SMD]"]
  R1 = Resistor [tolerance=±5% resistance=330 package="2512 [SMD]"]
  S2 = Momentary Switch [package=ksa_sealed_tac_switch]

nets:
  N1: Part1.GND, LED1.cathode
  N2: Part1.3V3, R1.Pin_1
  N3: S1.1, S2.3
  N4: S1.3, LED1.anode
  N5: R1.Pin_0, S2.2
