# Fritzing sketch button (saved by Fritzing 0.9.4)
breadboards: 1

parts:
  Part1 = Arduino Nano (Rev3.0)
  R1 = Resistor [tolerance=±5% resistance=10k package="2512 [SMD]"]
  S1 = Momentary Switch [package=ksa_sealed_tac_switch]

nets:
  N1: Part1.GND, R1.Pin_1
  N2: Part1.D2, R1.Pin_0, S1.4
  N3: Part1.3V3, S1.2
