# Fritzing sketch buttonLED (saved by Fritzing 0.9.4)
breadboards: 1

parts:
  Part1 = Arduino Nano (Rev3.0)
  LED1 = smd LED [color="Red (633nm)" package="1206 [SMD]"]
  R2 = Resistor [tolerance=±5% resistance=330 package="2512 [SMD]"]
  R1 = Resistor [tolerance=±5% resistance=10k package="2512 [SMD]"]
  S1 = Momentary Switch [package=ksa_sealed_tac_switch]

nets:
  N1: Part1.GND, R2.Pin_1, R1.Pin_1
  N2: Part1.D2, R1.Pin_0, S1.4
  N3: Part1.D12/MISO, LED1.anode
  N4: Part1.3V3, S1.2
  N5: LED1.cathode, R2.Pin_0
