# Fritzing sketch ldr (saved by Fritzing 0.9.4)
breadboards: 1

parts:
  Part1 = Arduino Nano (Rev3.0)
  R1 = Resistor [tolerance=±5% resistance=10k package="2512 [SMD]"]
  R2 = Photocell (LDR) [package=THT]

nets:
  N1: Part1.GND, R1.Pin_1
  N2: Part1.A0, R1.Pin_0, R2.pin_0
  N3: Part1.3V3, R2.pin_1
