# Fritzing sketch servo (saved by Fritzing 0.9.4)
breadboards: 1

parts:
  Part1 = Arduino Nano (Rev3.0)
  J1 = Basic Servo

nets:
  GND: Part1.GND, J1.gnd
  N1: Part1.D9, J1.pulse
  3V3: Part1.3V3, J1.vcc
