# Fritzing sketch etch-a-sketch (saved by Fritzing 0.9.4)
breadboards: 1

parts:
  Part1 = Arduino Nano (Rev3.0)
  U1 = POT [package=pot_alpha_rv16af-20]
  U2 = POT [package=pot_alpha_rv16af-20]

nets:
  N1: Part1.GND, U1.E, U2.E
  N2: Part1.A1, U2.S
  N3: Part1.A0, U1.S
  N4: Part1.3V3, U1.A, U2.A
