# Fritzing sketch pot (saved by Fritzing 0.9.4)
breadboards: 1

parts:
  Part1 = Arduino Nano (Rev3.0)
  U2 = POT [package=pot_alpha_rv16af-20]

nets:
  N1: Part1.GND, U2.E
  N2: Part1.A0, U2.S
  N3: Part1.3V3, U2.A
