# Fritzing sketch potLED (saved by Fritzing 0.9.4)
breadboards: 1

parts:
  Part1 = Arduino Nano (Rev3.0)
  U2 = POT [package=pot_alpha_rv16af-20]
  LED2 = smd LED [color="Red (633nm)" package="0805 [SMD]"]
  U3 = POT [package=pot_alpha_rv16af-20]
  R1 = Resistor [tolerance=±5% resistance=330 package="0805 [SMD]"]

nets:
  N1: Part1.GND, U2.E, U3.A, U3.E, R1.Pin_1
  N2: Part1.D12/MISO, LED2.anode
  N3: Part1.A1, U3.S
  N4: Part1.A0, U2.S
  N5: Part1.3V3, U2.A
  N6: LED2.cathode, R1.Pin_0
