# Fritzing sketch digitalInput (saved by Fritzing 0.9.4)
breadboards: 1

parts:
  LED3 = smd LED [color="Red (660nm)" package="0805 [SMD]"]
  Part2 = Arduino Nano (Rev3.0)
  S1 = Momentary Switch [package=ksa_sealed_tac_switch]
  R2 = Resistor [tolerance=±5% resistance=10k package=THT]
  R1 = Resistor [tolerance=±5% resistance=220 package=THT]

nets:
  N1: LED3.cathode, Part2.GND, R2.Pin_0
  N2: LED3.anode, R1.Pin_1
  N3: Part2.D2, R1.Pin_0
  N4: Part2.D3, S1.3, R2.Pin_1
  N5: Part2.5V, S1.2
