# Fritzing sketch digitalOutput (saved by Fritzing 0.9.4)
breadboards: 1

parts:
  R1 = Resistor [tolerance=±5% resistance=220 package=THT]
  LED3 = smd LED [color="Red (660nm)" package="0805 [SMD]"]
  Part2 = Arduino Nano (Rev3.0)

nets:
  N1: R1.Pin_0, LED3.anode
  N2: R1.Pin_1, Part2.D2
  N3: LED3.cathode, Part2.GND
