# Fritzing sketch passiveSeriesLED (saved by Fritzing 0.9.4)
breadboards: 1

parts:
  Part1 = Arduino Uno (Rev3)
  LED2 = smd LED [color="Red (660nm)" package="0805 [SMD]"]
  R1 = Resistor [tolerance=±5% resistance=220 package=THT]
  S1 = Pushbutton [package="[SMD]"]
  LED3 = smd LED [color="Red (660nm)" package="0805 [SMD]"]

nets:
  N1: Part1.GND, LED2.cathode
  N2: Part1.5V, R1.Pin_1
  N3: LED2.anode, LED3.cathode
  N4: R1.Pin_0, S1.Pin_1, S1.Pin_2
  N5: S1.Pin_3, S1.Pin_4, LED3.anode
